# Fritzing sketch breadboard (saved by Fritzing 0.9.4)
breadboards: 1

parts:
  Part2 = Arduino Motor Shield (Rev3)
  J1 = Screw terminal - 2 pins [package=THT]  # not connected
  J2 = Screw terminal - 2 pins [package=THT]  # not connected
  J3 = Screw terminal - 2 pins [package=THT]  # not connected
  J4 = Screw terminal - 2 pins [package=THT]  # not connected
  J5 = Screw terminal - 2 pins [package=THT]  # not connected
  J6 = Screw terminal - 2 pins [package=THT]  # not connected
  M2 = DC Motor
  M3 = DC Motor
  L1 = Solenoid
  Mod1 = KY-019 5V Relay Module [package="Breakout board"]

nets:
  N1: Part2.B-, M3.pin_2
  N2: Part2.B+, M3.pin_1
  N3: Part2.A-, M2.pin_2
  N4: Part2.A+, M2.pin_1
  N5: L1.pin1, Mod1.Common
  N6: L1.pin2, Mod1.NC

custom parts:
  KY-019 5V Relay Module: KY-019 5V Relay module, used to control AC circuits. (Special thanks to vanepp for fixing the PCB holes and other errors)
